// Logisim project ALU.circ as structural Verilog
module ALU (
  input  [31:0] A,
  input  [31:0] B,
  input  [4:0] Shift,
  input  CarryIn,
  input  [3:0] opcode,
  output [31:0] S,
  output [3:0] Flags
);

  wire alu_adc_1_c, alu_adc_1_n, alu_and_1_c, alu_and_1_n, alu_asr_1_c, alu_asr_1_n, alu_eor_1_c,
       alu_eor_1_n, alu_lsl_1_c, alu_lsl_1_n, alu_lsr_1_c, alu_lsr_1_n, alu_sbc_1_c, alu_sbc_1_n;
  wire [31:0] ALU_ADC_T, ALU_AND_T, ALU_ASR_T, ALU_BIC_T, ALU_CMN_T, ALU_CMP_T, ALU_EOR_T, ALU_LSL_T,
       ALU_LSR_T, ALU_MUL_T, ALU_MVN_T, ALU_ORR_T, ALU_ROR_T, ALU_RSB_T, ALU_SBC_T, ALU_TST_T;

  ALU_AND alu_and_1 (.A(A), .B(B), .S(ALU_AND_T), .N(alu_and_1_n), .C(alu_and_1_c));  // open: Z
  ALU_LSR alu_lsr_1 (.A(A), .Shift(Shift), .S(ALU_LSR_T), .N(alu_lsr_1_n), .C(alu_lsr_1_c));  // open: Z
  ALU_SBC alu_sbc_1 (.A(A), .Cin(CarryIn), .B(B), .S(ALU_SBC_T), .N(alu_sbc_1_n), .C(alu_sbc_1_c));  // open: Z, V
  ALU_EOR alu_eor_1 (.A(A), .B(B), .S(ALU_EOR_T), .N(alu_eor_1_n), .C(alu_eor_1_c));  // open: Z
  ALU_ASR alu_asr_1 (.A(A), .Shift(Shift), .S(ALU_ASR_T), .N(alu_asr_1_n), .C(alu_asr_1_c));  // open: Z
  ALU_LSL alu_lsl_1 (.A(A), .Shift(Shift), .S(ALU_LSL_T), .N(alu_lsl_1_n), .C(alu_lsl_1_c));  // open: Z
  ALU_ADC alu_adc_1 (.A(A), .Cin(CarryIn), .B(B), .S(ALU_ADC_T), .N(alu_adc_1_n), .C(alu_adc_1_c));  // open: Z, V
  Multiplexer #(.select(4), .width(32)) multiplexer_1 (
    .in0(ALU_AND_T), .in1(ALU_EOR_T), .in2(ALU_LSL_T), .in3(ALU_LSR_T), .in4(ALU_ASR_T), .in5(ALU_ADC_T),
    .in6(ALU_SBC_T), .in7(ALU_ROR_T), .in8(ALU_TST_T), .in9(ALU_RSB_T), .in10(ALU_CMP_T), .in11(ALU_CMN_T),
    .in12(ALU_ORR_T), .in13(ALU_MUL_T), .in14(ALU_BIC_T), .in15(ALU_MVN_T), .out(S), .sel(opcode));

  // Other names for the same wires on the sheet: Cin = CarryIn; C = Flags[0]; V = Flags[1]; N = Flags[2];
  //   Z = Flags[3]

  // Notes on the sheet:
  //   Note: for ROR, C = N
  //   Note 2: assume that shift > 0 for LSL and LSR
endmodule

module Z_flag (
  input  [31:0] I,
  output O
);

  wire and_1_out, and_2_out;
  wire [3:0] nor_1_out, nor_2_out;

  assign nor_1_out = ~(I[3:0] | I[7:4] | I[11:8] | I[15:12]);  // NOR_Gate nor_1, 4 bits wide
  assign nor_2_out = ~(I[19:16] | I[23:20] | I[27:24] | I[31:28]);  // NOR_Gate nor_2, 4 bits wide
  and and_1 (and_1_out, nor_1_out[0], nor_1_out[1], nor_1_out[2], nor_1_out[3]);
  and and_2 (and_2_out, nor_2_out[0], nor_2_out[1], nor_2_out[2], nor_2_out[3]);
  and and_3 (O, and_1_out, and_2_out);
endmodule

module N_flag (
  input  [31:0] I,
  output O
);

  BitSelector #(.width(32)) bitselector_1 (.in(I), .out(O), .sel({5{1'b1}}));
endmodule

module ALU_AND (
  input  [31:0] A,
  input  [31:0] B,
  output [31:0] S,
  output Z,
  output N,
  output C
);

  assign S = A & B;  // AND_Gate and_1, 32 bits wide
  Z_flag z_flag_1 (.I(S), .O(Z));
  N_flag n_flag_1 (.I(S), .O(N));

  assign C = 1'b0;
endmodule

module ALU_EOR (
  input  [31:0] A,
  input  [31:0] B,
  output [31:0] S,
  output Z,
  output N,
  output C
);

  wire [31:0] and_1_out, and_2_out, not_1_out, not_2_out;

  assign and_1_out = A & not_1_out;  // AND_Gate and_1, 32 bits wide
  assign not_1_out = ~B;  // NOT_Gate not_1, 32 bits wide
  assign not_2_out = ~A;  // NOT_Gate not_2, 32 bits wide
  assign and_2_out = not_2_out & B;  // AND_Gate and_2, 32 bits wide
  assign S = and_1_out | and_2_out;  // OR_Gate or_1, 32 bits wide
  Z_flag z_flag_1 (.I(S), .O(Z));
  N_flag n_flag_1 (.I(S), .O(N));

  assign C = 1'b0;
endmodule

module ALU_LSL (
  input  [31:0] A,
  input  [4:0] Shift,
  output [31:0] S,
  output Z,
  output N,
  output C
);

  wire [4:0] subtractor_1_out;

  Shifter #(.width(32)) shifter_1 (.in(A), .\dist (Shift), .out(S));
  Subtractor #(.width(5)) subtractor_1 (.a({5{1'b0}}), .b(Shift), .out(subtractor_1_out));  // open: bin, bout
  Z_flag z_flag_1 (.I(S), .O(Z));
  N_flag n_flag_1 (.I(S), .O(N));
  BitSelector #(.width(32)) bitselector_1 (.in(A), .out(C), .sel(subtractor_1_out));
endmodule

module ALU_LSR (
  input  [31:0] A,
  input  [4:0] Shift,
  output [31:0] S,
  output Z,
  output N,
  output C
);

  wire [4:0] subtractor_1_out;

  Shifter #(.shift("lr"), .width(32)) shifter_1 (.in(A), .\dist (Shift), .out(S));
  Subtractor #(.width(5)) subtractor_1 (.a(Shift), .b(5'b00001), .out(subtractor_1_out));  // open: bin, bout
  Z_flag z_flag_1 (.I(S), .O(Z));
  N_flag n_flag_1 (.I(S), .O(N));
  BitSelector #(.width(32)) bitselector_1 (.in(A), .out(C), .sel(subtractor_1_out));
endmodule

module ALU_ASR (
  input  [31:0] A,
  input  [4:0] Shift,
  output [31:0] S,
  output Z,
  output N,
  output C
);

  wire [4:0] subtractor_1_out;

  Shifter #(.shift("ar"), .width(32)) shifter_1 (.in(A), .\dist (Shift), .out(S));
  Subtractor #(.width(5)) subtractor_1 (.a(Shift), .b(5'b00001), .out(subtractor_1_out));  // open: bin, bout
  Z_flag z_flag_1 (.I(S), .O(Z));
  N_flag n_flag_1 (.I(S), .O(N));
  BitSelector #(.width(32)) bitselector_1 (.in(A), .out(C), .sel(subtractor_1_out));
endmodule

module ALU_ADC (
  input  [31:0] A,
  input  Cin,
  input  [31:0] B,
  output [31:0] S,
  output Z,
  output N,
  output C,
  output V
);

  wire and_1_out, n_flag_1_o, n_flag_2_o, not_1_out, not_2_out;

  N_flag n_flag_1 (.I(A), .O(n_flag_1_o));
  not not_1 (not_1_out, n_flag_1_o);
  and and_1 (and_1_out, not_1_out, not_2_out);
  Adder #(.width(32)) adder_1 (.a(A), .b(B), .out(S), .cin(Cin), .cout(C));
  N_flag n_flag_2 (.I(B), .O(n_flag_2_o));
  not not_2 (not_2_out, n_flag_2_o);
  Z_flag z_flag_1 (.I(S), .O(Z));
  N_flag n_flag_3 (.I(S), .O(N));
  and and_2 (V, N, and_1_out);
endmodule

module ALU_SBC (
  input  [31:0] A,
  input  Cin,
  input  [31:0] B,
  output [31:0] S,
  output Z,
  output N,
  output C,
  output V
);

  wire and_1_out, n_flag_1_o, n_flag_2_o, not_1_out, subtractor_1_bout;

  N_flag n_flag_1 (.I(A), .O(n_flag_1_o));
  not not_1 (not_1_out, n_flag_1_o);
  and and_1 (and_1_out, not_1_out, n_flag_2_o);
  Subtractor #(.width(32)) subtractor_1 (.a(A), .b(B), .out(S), .bin(Cin), .bout(subtractor_1_bout));
  N_flag n_flag_2 (.I(B), .O(n_flag_2_o));
  Z_flag z_flag_1 (.I(S), .O(Z));
  N_flag n_flag_3 (.I(S), .O(N));
  not not_2 (C, subtractor_1_bout);
  and and_2 (V, N, and_1_out);
endmodule
