// Logisim project Ctl_Conditional.circ as structural Verilog: 1 circuit, main circuit Conditional
module Conditional (
  input  Enable,
  input  [15:0] Instruction,
  input  Z,
  input  C,
  input  N,
  input  V,
  output Verified,
  output [10:0] Offset
);

  wire HI, not_1_out, not_2_out, not_3_out, not_4_out, not_5_out;

  not not_1 (not_1_out, Z);
  not not_2 (not_2_out, C);
  not not_3 (not_3_out, N);
  not not_4 (not_4_out, V);
  Multiplexer #(.select(4)) multiplexer_1 (
    .in0(Z), .in1(not_1_out), .in2(C), .in3(not_2_out), .in4(N), .in5(not_3_out), .in6(V), .in7(not_4_out),
    .in8(HI), .sel(Instruction[11:8]));  // open: in9, in10, in11, in12, in13, in14, in15, out
  not not_5 (not_5_out, Z);
  and and_1 (HI, C, not_5_out);

  assign Verified = Enable;
endmodule
