// Logisim project Ctl_Flags_APSR.circ as structural Verilog: 1 circuit, main circuit Flags_APSR
module Flags_APSR (
  input  [3:0] Update_Mask,
  input  [3:0] Flags_In,
  input  Rst,
  input  Clk,
  output [3:0] Flags_Out
);

  wire [3:0] and_1_out, and_2_out, not_1_out, old_flag;

  assign and_1_out = old_flag & not_1_out;  // AND_Gate and_1, 4 bits wide
  assign not_1_out = ~Update_Mask;  // NOT_Gate not_1, 4 bits wide
  assign and_2_out = Update_Mask & Flags_In;  // AND_Gate and_2, 4 bits wide
  assign Flags_Out = and_1_out | and_2_out;  // OR_Gate or_1, 4 bits wide
  D_Flip_Flop d_ff_1 (.D(Flags_Out[0]), .clk(Clk), .Q(old_flag[0]), .reset(Rst));  // open: Qn, preset
  D_Flip_Flop d_ff_2 (.D(Flags_Out[1]), .clk(Clk), .Q(old_flag[1]), .reset(Rst));  // open: Qn, preset
  D_Flip_Flop d_ff_3 (.D(Flags_Out[2]), .clk(Clk), .Q(old_flag[2]), .reset(Rst));  // open: Qn, preset
  D_Flip_Flop d_ff_4 (.D(Flags_Out[3]), .clk(Clk), .Q(old_flag[3]), .reset(Rst));  // open: Qn, preset
endmodule
