// Logisim project Ctl_Load_Store.circ as structural Verilog: 1 circuit, main circuit Load_Store
module Load_Store (
  input  Enable,
  input  [15:0] Instruction,
  input  Clk,
  input  Reset,
  input  [31:0] Stack_Pointer,
  output Store,
  output [2:0] Rmd,
  output Load,
  output [31:0] RAM_Addr,
  output PC_Hold
);

  wire and_1_out, and_2_out, and_3_out, d_ff_1_q, d_ff_1_qn, not_1_out, not_2_out, or_1_out;
  wire [31:0] adder_1_out, imm8;

  Multiplexer multiplexer_1 (.in0(1'b0), .in1(not_1_out), .out(Store), .sel(Enable));
  not not_1 (not_1_out, Instruction[11]);
  D_Flip_Flop #(.trigger("falling")) d_ff_1 (
    .D(and_1_out), .clk(Clk), .Q(d_ff_1_q), .Qn(d_ff_1_qn), .reset(or_1_out));  // open: preset
  and and_1 (and_1_out, ~d_ff_1_q, Instruction[11]);  // AND_Gate
  or or_1 (or_1_out, Reset, not_2_out);
  not not_2 (not_2_out, Enable);
  assign imm8 = {{24{Instruction[7]}}, Instruction[7:0]};  // Bit_Extender bit_extender_1
  and and_2 (and_2_out, d_ff_1_q, Instruction[11]);
  and and_3 (and_3_out, Instruction[11], d_ff_1_qn);
  Multiplexer multiplexer_2 (.in0(1'b0), .in1(and_2_out), .out(Load), .sel(Enable));
  Multiplexer multiplexer_3 (.in0(1'b0), .in1(and_3_out), .out(PC_Hold), .sel(Enable));
  Adder #(.width(32)) adder_1 (.a(Stack_Pointer), .b(imm8), .out(adder_1_out));  // open: cin, cout
  Multiplexer #(.width(3)) multiplexer_4 (.in0(3'b000), .in1(Instruction[10:8]), .out(Rmd), .sel(Enable));
  Multiplexer #(.width(32)) multiplexer_5 (.in0({32{1'b0}}), .in1(adder_1_out), .out(RAM_Addr), .sel(Enable));

  // Other names for the same wires on the sheet: E1 = Enable; Rt[2:0] = Instruction[10:8]; Inst = Instruction[11];
  //   SP[31:0] = Stack_Pointer

  // Notes on the sheet:
  //   Instruction: pull=down
  //   Delay load and hold PC for 1 cycle for the RAM to send out requested data 
endmodule
