// Logisim project Ctl_Shift_Add_Sub_Mov.circ as structural Verilog
module Shift_Add_Sub_Mov (
  input  Enable,
  input  [15:0] Instruction,
  output [3:0] ALU_Opcode,
  output [31:0] Imm32,
  output Imm32_Enable,
  output [4:0] Imm5,
  output [3:0] Flags_Update_Mask,
  output [2:0] Rm,
  output Carry,
  output [2:0] Rn,
  output [2:0] Rd
);

  wire bit13, C_Mask, Enable_t, multiplexer_3_out, V_Mask;
  wire [2:0] E3;
  wire [3:0] ALU_Opcode_t, E4, multiplexer_12_out;
  wire [4:0] E5;
  wire [13:6] Instruction_t;
  wire [31:0] bit_extender_1_out, bit_extender_2_out, E32;

  Multiplexer #(.select(4)) multiplexer_1 (
    .in0(1'b1), .in1(1'b1), .in2(1'b1), .in3(1'b1), .in4(1'b1), .in5(1'b1), .in6(1'b1), .in7(1'b1),
    .in8(1'b1), .in9(1'b1), .in10(1'b1), .in11(1'b1), .in12(1'b1), .in13(1'b0), .in14(1'b1), .in15(1'b1),
    .out(C_Mask), .sel(ALU_Opcode_t));
  Multiplexer #(.select(3), .width(4)) multiplexer_2 (
    .in0(4'b0010), .in1(4'b0000), .in2(multiplexer_12_out), .in3(4'b0000), .in4(4'b0000), .in5(4'b0000),
    .in6(4'b0000), .in7(4'b0000), .out(ALU_Opcode_t), .sel(Instruction_t[13:11]));
  Bit_Extender #(.in_width(3), .out_width(32)) bit_extender_1 (.out(bit_extender_1_out));  // open: in
  Bit_Extender #(.out_width(32)) bit_extender_2 (.out(bit_extender_2_out));  // open: in
  // AND_Gate and_1 has open pins: in0=ALU_Opcode_t, in1={2'b11, C_Mask, V_Mask}, out=open
  Multiplexer #(.select(4)) multiplexer_3 (
    .out(multiplexer_3_out), .sel(ALU_Opcode_t));  // open: in0, in1, in2, in3, in4, in5, in6, in7, in8, in9, in10, in11, in12, in13, in14, in15
  Multiplexer multiplexer_4 ();  // open: in0, in1, out, sel
  Multiplexer #(.width(32)) multiplexer_5 (
    .in0(bit_extender_1_out), .in1(bit_extender_2_out), .out(Imm32), .sel(bit13));
  // Multiplexer multiplexer_6: pin names not known; wires that end beside it: Instruction_t[10:6], Enable_t
  Multiplexer multiplexer_7 ();  // open: in0, in1, out, sel
  Multiplexer multiplexer_8 ();  // open: in0, in1, out, sel
  Multiplexer #(.select(4)) multiplexer_9 (
    .in0(1'b0), .in1(1'b0), .in2(1'b0), .in3(1'b0), .in4(1'b0), .in5(1'b1), .in6(1'b1), .in7(1'b0),
    .in8(1'b0), .in9(1'b1), .in10(1'b1), .in11(1'b1), .in12(1'b0), .in13(1'b0), .in14(1'b0), .in15(1'b0),
    .out(V_Mask), .sel(ALU_Opcode_t));
  Multiplexer #(.width(3)) multiplexer_10 (.out(Rm));  // open: in0, in1, sel
  Multiplexer multiplexer_11 ();  // open: in0, in1, out, sel
  Multiplexer #(.select(2), .width(4)) multiplexer_12 (
    .in0(4'b0101), .in1(4'b0110), .in2(4'b0101), .in3(4'b0110), .out(multiplexer_12_out),
    .sel(Instruction_t[10:9]));
  assign E4 = {{3{Enable}}, Enable};  // Bit_Extender bit_extender_3
  assign E3 = {{2{Enable}}, Enable};  // Bit_Extender bit_extender_4
  assign E32 = {{31{Enable}}, Enable};  // Bit_Extender bit_extender_5
  assign E5 = {{4{Enable}}, Enable};  // Bit_Extender bit_extender_6

  // Other names for the same wires on the sheet: tenine[1:0] = Instruction_t[10:9]

  // Notes on the sheet:
  //   Pull output low on Enable = 0
  //   only ADD and SUB use Rm
  //   Enable carry for SUB since it is reversed in ALU
  //   ALU will use Imm32 instead of Rm
  //   Note 3: Imm32_Enable forces the use of the immediate for Rm register
  //   Note: ALU uses Rn register for shifts. Use Rn instead of Rm for shifts (immediate) here too
  //   Note 2: MOV uses RSB ALU opcode with Imm8 reversed so that it is copied to output register
endmodule

module Alu_Opcode (
  input  thirteen,
  input  twelve,
  input  eleven,
  input  ten,
  input  nine,
  output first,
  output second,
  output third,
  output forth
);

  wire and_2_out, and_3_out, and_4_out, and_5_out, and_6_out, and_7_out, not_1_out, not_2_out, not_3_out,
       not_4_out;

  not not_1 (not_1_out, thirteen);
  not not_2 (not_2_out, twelve);
  not not_3 (not_3_out, eleven);
  not not_4 (not_4_out, nine);
  and and_1 (first, thirteen, not_2_out);
  and and_2 (and_2_out, thirteen, not_3_out);
  and and_3 (and_3_out, eleven, nine);
  and and_4 (and_4_out, thirteen, eleven);
  and and_5 (and_5_out, thirteen, not_3_out);
  and and_6 (and_6_out, not_1_out, not_2_out, eleven);
  and and_7 (and_7_out, not_1_out, eleven, not_4_out);
  or or_1 (second, twelve, and_2_out);
  or or_2 (third, not_2_out, and_3_out, and_4_out);
  or or_3 (forth, and_5_out, and_6_out, and_7_out);
endmodule
